// Logisim project DECODER_2_4_CIRCUIT.circ as structural Verilog: 1 circuit, main circuit main
module main (
  input  S,
  input  A,
  output out_3,
  output out_4,
  output out_5,
  output out_6
);

  wire not_1_out, not_2_out, not_3_out, not_4_out;

  and and_1 (out_3, S, A);
  and and_2 (out_4, S, not_1_out);
  not not_1 (not_1_out, A);
  not not_2 (not_2_out, S);
  and and_3 (out_5, not_2_out, A);
  not not_3 (not_3_out, S);
  and and_4 (out_6, not_3_out, not_4_out);
  not not_4 (not_4_out, A);
endmodule
