// Logisim project FEEDBACK_LOOP.circ as structural Verilog: 1 circuit, main circuit main
module main (
  input  S,
  input  R,
  output out_3
);

  wire and_1_out, nor_1_out;

  nor nor_1 (nor_1_out, S, and_1_out);
  and and_1 (and_1_out, out_3, R);
  not not_1 (out_3, nor_1_out);
endmodule
