// Logisim project FULL_ADDER.circ as structural Verilog: 1 circuit, main circuit main
module main (
  input  A_3,
  input  B_3,
  input  A_2,
  input  B_2,
  input  A_1,
  input  B_1,
  input  A_0,
  input  B_0,
  input  Cin,
  output out_10,
  output out_11,
  output out_12,
  output out_13,
  output SOMA
);

  wire and_1_out, and_2_out, and_3_out, and_4_out, and_5_out, and_6_out, C1_out, C2_out, COUT_out, or_1_out,
       or_2_out, S1_out, xor_1_out, xor_2_out, xor_4_out;

  and C1 (C1_out, A_0, B_0);
  xor S1 (S1_out, A_0, B_0);
  and and_1 (and_1_out, A_1, B_1);
  xor xor_1 (xor_1_out, A_1, B_1);
  and C2 (C2_out, S1_out, Cin);
  xor S2 (SOMA, S1_out, Cin);
  and and_2 (and_2_out, A_2, B_2);
  xor xor_2 (xor_2_out, A_2, B_2);
  and and_3 (and_3_out, xor_1_out, COUT_out);
  xor xor_3 (out_13, xor_1_out, COUT_out);
  or COUT (COUT_out, C1_out, C2_out);
  or or_1 (or_1_out, and_1_out, and_3_out);
  and and_4 (and_4_out, A_3, B_3);
  xor xor_4 (xor_4_out, A_3, B_3);
  or or_2 (or_2_out, and_2_out, and_5_out);
  and and_5 (and_5_out, xor_2_out, or_1_out);
  xor xor_5 (out_12, xor_2_out, or_1_out);
  or or_3 (out_10, and_4_out, and_6_out);
  and and_6 (and_6_out, xor_4_out, or_2_out);
  xor xor_6 (out_11, xor_4_out, or_2_out);
endmodule
