// Logisim project GT_EQ_LT_CIRCUIT.circ as structural Verilog: 1 circuit, main circuit main
module main (
  input  A,
  input  B,
  output A_GT_B,
  output B_GT_A,
  output A_EQ_B
);

  wire not_1_out, not_2_out, xor_1_out;

  not not_1 (not_1_out, B);
  not not_2 (not_2_out, A);
  and and_1 (A_GT_B, A, not_1_out);
  and and_2 (B_GT_A, not_2_out, B);
  xor xor_1 (xor_1_out, A, B);
  not not_3 (A_EQ_B, xor_1_out);
endmodule
