// Logisim project HALF_ADDER.circ as structural Verilog: 1 circuit, main circuit main
module main (
  input  A,
  input  B,
  output out_3,
  output out_4
);

  and C (out_3, A, B);
  xor S (out_4, A, B);
endmodule
