// Logisim project MULTIPLEXER_CIRCUIT.circ as structural Verilog: 1 circuit, main circuit main
module main (
  input  S,
  input  A,
  input  B,
  output out_4
);

  wire and_1_out, and_2_out, not_1_out;

  not not_1 (not_1_out, S);
  and and_1 (and_1_out, S, A);
  or or_1 (out_4, and_1_out, and_2_out);
  and and_2 (and_2_out, not_1_out, B);
endmodule
