// Logisim project REGISTERS_CIRCUIT.circ as structural Verilog: 1 circuit, main circuit main
module main (
  input  A0_0,
  input  A0_1,
  input  A0_2,
  input  A0_3,
  input  in_5,
  output out_6,
  output BIT_0,
  output BIT_1,
  output BIT_2,
  output BIT_3
);

  wire and_1_out, and_2_out, and_3_out, and_4_out, and_5_out, and_6_out, and_7_out, and_8_out, C,
       clock_1_out, nor_2_out, nor_3_out, nor_6_out, nor_7_out, nor_10_out, not_1_out, not_2_out, not_3_out,
       not_4_out, not_5_out, R_out, S_out;

  Clock clock_1 (.out(clock_1_out));
  not not_1 (not_1_out, in_5);
  and and_1 (and_1_out, clock_1_out, in_5);
  nor nor_1 (out_6, and_2_out, nor_2_out);
  and and_2 (and_2_out, clock_1_out, not_1_out);
  nor nor_2 (nor_2_out, and_1_out, out_6);
  Clock clock_2 (.out(C));
  and R (R_out, C, not_2_out);
  not not_2 (not_2_out, A0_0);
  and S (S_out, C, A0_0);
  nor nor_3 (nor_3_out, S_out, BIT_0);
  nor nor_4 (BIT_0, R_out, nor_3_out);
  not not_3 (not_3_out, A0_1);
  and and_3 (and_3_out, C, not_3_out);
  nor nor_5 (BIT_1, and_3_out, nor_6_out);
  and and_4 (and_4_out, C, A0_1);
  and and_5 (and_5_out, C, not_4_out);
  nor nor_6 (nor_6_out, and_4_out, BIT_1);
  not not_4 (not_4_out, A0_2);
  and and_6 (and_6_out, C, A0_2);
  nor nor_7 (nor_7_out, and_6_out, BIT_2);
  nor nor_8 (BIT_2, and_5_out, nor_7_out);
  not not_5 (not_5_out, A0_3);
  and and_7 (and_7_out, C, not_5_out);
  nor nor_9 (BIT_3, and_7_out, nor_10_out);
  and and_8 (and_8_out, C, A0_3);
  nor nor_10 (nor_10_out, and_8_out, BIT_3);
endmodule
