// Logisim project SR_LATCH.circ as structural Verilog: 1 circuit, main circuit main
module main (
  input  R,
  input  S,
  output out_3
);

  wire not_1_out, or_1_out, or_2_out;

  or or_1 (or_1_out, R, not_1_out);
  not not_1 (not_1_out, or_2_out);
  or or_2 (or_2_out, out_3, S);
  not not_2 (out_3, or_1_out);
endmodule
